// Logisim project 171044036_project1.circ as structural Verilog: 1 circuit, main circuit main
module main (
);

  wire and_1_out, and_2_out, and_4_out, and_5_out, and_7_out, and_8_out, and_10_out, and_11_out, and_12_out,
       and_14_out, and_15_out, and_16_out, and_17_out, and_18_out, and_19_out, and_20_out, and_21_out,
       and_22_out, and_23_out, and_24_out, and_25_out, and_26_out, and_27_out, and_28_out, and_29_out,
       and_30_out, and_31_out, and_32_out, and_33_out, clock_1_out, clock_2_out, clock_3_out, clock_4_out,
       clock_5_out, decoder_1_out0, decoder_1_out1, decoder_1_out2, decoder_1_out3, decoder_1_out4,
       decoder_1_out5, decoder_1_out7, nand_1_out, not_1_out, not_2_out, not_3_out, not_4_out, not_5_out,
       not_6_out, not_7_out, not_8_out, not_9_out, not_10_out, not_11_out, not_12_out, not_13_out,
       not_14_out, not_15_out, not_16_out, not_17_out, not_18_out, not_19_out, not_20_out, not_21_out,
       not_22_out, not_23_out, not_24_out, not_25_out, not_26_out, not_27_out, not_28_out, not_29_out,
       not_30_out, not_31_out, not_32_out, not_33_out, not_34_out, not_35_out, not_36_out, not_37_out,
       not_38_out, not_39_out, or_5_out, or_6_out, or_7_out, or_8_out, or_9_out, or_10_out, or_11_out,
       p1_2_out, p1_out, p2_2_out, p2_out, r_2_out, r_out, xnor_1_out;
  wire [1:0] and_3_out, and_6_out, and_9_out, and_13_out, register_1_q, register_2_q, register_3_q,
       register_4_q;
  wire [2:0] n2_out, register_5_q, s0_out;
  wire [3:0] counter_1_q, counter_2_q;

  Clock clock_1 (.out(clock_1_out));
  Clock clock_2 (.out(clock_2_out));
  Clock clock_3 (.out(clock_3_out));
  not not_1 (not_1_out, register_1_q[1]);
  not not_2 (not_2_out, register_1_q[1]);
  not not_3 (not_3_out, register_1_q[0]);
  not not_4 (not_4_out, register_1_q[1]);
  not not_5 (not_5_out, register_1_q[0]);
  Register #(.width(2)) register_1 (.D(and_3_out), .en(1'b1), .Q(register_1_q), .clk(clock_3_out));  // open: clr
  not not_6 (not_6_out, register_2_q[1]);
  not not_7 (not_7_out, register_2_q[1]);
  not not_8 (not_8_out, register_2_q[0]);
  not not_9 (not_9_out, register_2_q[1]);
  not not_10 (not_10_out, register_2_q[0]);
  Register #(.width(2)) register_2 (.D(and_6_out), .en(1'b1), .Q(register_2_q), .clk(clock_1_out));  // open: clr
  not not_11 (not_11_out, register_3_q[1]);
  not not_12 (not_12_out, register_3_q[1]);
  not not_13 (not_13_out, register_3_q[0]);
  not not_14 (not_14_out, register_3_q[1]);
  not not_15 (not_15_out, register_3_q[0]);
  Register #(.width(2)) register_3 (.D(and_9_out), .en(1'b1), .Q(register_3_q), .clk(clock_2_out));  // open: clr
  and r (r_out, not_1_out, register_1_q[0]);
  and and_1 (and_1_out, r_2_out, not_2_out, register_1_q[0]);
  and and_2 (and_2_out, r_2_out, not_3_out, register_1_q[1]);
  and and_3 (and_3_out[0], r_2_out, not_4_out, not_5_out);
  Clock clock_4 (.out(clock_4_out));
  and p1 (p1_out, not_6_out, register_2_q[0]);
  and and_4 (and_4_out, p1_2_out, not_7_out, register_2_q[0]);
  and and_5 (and_5_out, p1_2_out, not_8_out, register_2_q[1]);
  and and_6 (and_6_out[0], p1_2_out, not_9_out, not_10_out);
  and p2 (p2_out, not_11_out, register_3_q[0]);
  and and_7 (and_7_out, p2_2_out, not_12_out, register_3_q[0]);
  and and_8 (and_8_out, p2_2_out, not_13_out, register_3_q[1]);
  and and_9 (and_9_out[0], p2_2_out, not_14_out, not_15_out);
  or or_1 (and_3_out[1], and_1_out, and_2_out);
  Register #(.width(2)) register_4 (.D(and_13_out), .en(1'b1), .Q(register_4_q), .clk(clock_4_out));  // open: clr
  or or_2 (and_6_out[1], and_4_out, and_5_out);
  or or_3 (and_9_out[1], and_7_out, and_8_out);
  not not_16 (not_16_out, register_4_q[1]);
  not not_17 (not_17_out, register_4_q[1]);
  not not_18 (not_18_out, register_4_q[0]);
  not not_19 (not_19_out, register_4_q[1]);
  not not_20 (not_20_out, register_4_q[0]);
  and and_10 (and_10_out, not_16_out, register_4_q[0]);
  and and_11 (and_11_out, 1'b1, not_17_out, register_4_q[0]);
  and and_12 (and_12_out, 1'b1, not_18_out, register_4_q[1]);
  and and_13 (and_13_out[0], 1'b1, not_19_out, not_20_out);
  or or_4 (and_13_out[1], and_11_out, and_12_out);
  not not_21 (not_21_out, and_10_out);
  xnor xnor_1 (xnor_1_out, p1_out, p2_out);
  not not_22 (not_22_out, p2_out);
  and and_14 (and_14_out, not_22_out, p1_out);
  not not_23 (not_23_out, p1_out);
  not not_24 (not_24_out, p2_out);
  not not_25 (not_25_out, p1_out);
  not not_26 (not_26_out, p2_out);
  not not_27 (not_27_out, xnor_1_out);
  and and_15 (and_15_out, p2_out, p1_out);
  and and_16 (and_16_out, not_23_out, not_24_out);
  and and_17 (and_17_out, not_25_out, p2_out);
  and and_18 (and_18_out, p1_out, not_26_out);
  Clock clock_5 (.out(clock_5_out));
  or s0 (s0_out[0], register_5_q[0], and_10_out);
  or s1 (s0_out[1], register_5_q[1], and_10_out);
  and s2 (s0_out[2], register_5_q[2], not_21_out);
  not not_28 (not_28_out, s0_out[0]);
  not not_29 (not_29_out, s0_out[1]);
  not not_30 (not_30_out, s0_out[2]);
  not not_31 (not_31_out, s0_out[0]);
  not not_32 (not_32_out, s0_out[1]);
  not not_33 (not_33_out, s0_out[2]);
  or or_5 (or_5_out, and_15_out, and_16_out, and_17_out);
  or or_6 (or_6_out, and_15_out, and_16_out, and_18_out);
  Register #(.width(3)) register_5 (.D(n2_out), .en(1'b1), .Q(register_5_q), .clk(clock_5_out));  // open: clr
  not not_34 (not_34_out, p2_out);
  and and_19 (and_19_out, not_30_out, s0_out[1]);
  and and_20 (and_20_out, not_29_out, s0_out[2]);
  and and_21 (and_21_out, not_28_out, not_29_out, not_30_out);
  and and_22 (and_22_out, s0_out[2], not_29_out, s0_out[0], and_14_out);
  and and_23 (and_23_out, s0_out[0], and_17_out);
  and and_24 (and_24_out, not_31_out, and_18_out);
  and and_25 (and_25_out, not_31_out, not_32_out, not_33_out);
  and and_26 (and_26_out, not_31_out, not_32_out, s0_out[2], or_5_out);
  and and_27 (and_27_out, s0_out[0], not_32_out, or_6_out);
  not not_35 (not_35_out, p1_out);
  not not_36 (not_36_out, s0_out[2]);
  and and_28 (and_28_out, p2_out, not_35_out, not_36_out, s0_out[1], s0_out[0]);
  and and_29 (and_29_out, s0_out[2], s0_out[0]);
  not not_37 (not_37_out, s0_out[1]);
  and and_30 (and_30_out, s0_out[2], not_37_out, not_38_out, nand_1_out);
  not not_38 (not_38_out, s0_out[0]);
  nand nand_1 (nand_1_out, not_34_out, p1_out);
  or or_7 (or_7_out, and_19_out, and_20_out);
  or or_8 (or_8_out, and_23_out, and_24_out);
  not not_39 (not_39_out, r_out);
  or or_9 (or_9_out, and_28_out, and_29_out, and_30_out);
  and and_31 (and_31_out, not_30_out, s0_out[0], not_27_out);
  and and_32 (and_32_out, or_7_out, xnor_1_out, not_28_out);
  and and_33 (and_33_out, not_33_out, s0_out[1], or_8_out);
  or or_10 (or_10_out, and_33_out, and_25_out, and_26_out, and_27_out);
  and n0 (n2_out[2], not_39_out, or_9_out);
  or or_11 (or_11_out, and_31_out, and_32_out, and_21_out, and_22_out);
  nand n2 (n2_out[0], or_11_out, not_39_out);
  nand n1 (n2_out[1], or_10_out, not_39_out);
  LED led_1 (.in(decoder_1_out1));
  LED led_2 (.in(decoder_1_out2));
  LED led_3 (.in(decoder_1_out0));
  Counter #(.width(4), .max('hf)) counter_1 (
    .Q(counter_1_q), .clk(decoder_1_out0));  // open: load, D, count, carry, clr
  LED led_4 (.in(decoder_1_out4));
  LED led_5 (.in(decoder_1_out3));
  Decoder #(.select(3)) decoder_1 (
    .out0(decoder_1_out0), .out1(decoder_1_out1), .out2(decoder_1_out2), .out3(decoder_1_out3),
    .out4(decoder_1_out4), .out5(decoder_1_out5), .out7(decoder_1_out7), .sel(s0_out), .en(1'b1));  // open: out6
  Hex_Digit_Display hex_digit_display_1 (.value(counter_1_q));  // open: dp
  Button p1_2 (.out(p1_2_out));
  Button r_2 (.out(r_2_out));
  LED led_6 (.in(decoder_1_out5));
  LED led_7 (.in(decoder_1_out7));
  Hex_Digit_Display hex_digit_display_2 (.value(counter_2_q));  // open: dp
  Button p2_2 (.out(p2_2_out));
  Counter #(.width(4), .max('hf)) counter_2 (
    .Q(counter_2_q), .clk(decoder_1_out7));  // open: load, D, count, carry, clr
endmodule
