// Logisim project cu.circ as structural Verilog: 1 circuit, main circuit main
module main (
  input  clk,
  input  eq,
  input  lt,
  input  gr,
  input  eq1,
  input  go,
  output mr,
  output lb,
  output lx,
  output la,
  output _2s,
  output mx,
  output [3:0] state,
  output lm,
  output sm,
  output md,
  output sa,
  output lr,
  output dx
);

  wire and_6_out, and_8_out, and_9_out, and_10_out, and_11_out, and_12_out, and_13_out, and_14_out,
       and_15_out, and_16_out, and_17_out, and_18_out, and_19_out, and_20_out, and_21_out, and_22_out,
       not_1_out, not_2_out, not_3_out, not_4_out, not_5_out, not_6_out, not_7_out, not_8_out, not_9_out,
       or_9_out;
  wire [3:0] or_7_out;

  or or_1 (la, lb, _2s, md);
  or or_2 (lm, lb, sm);
  or or_3 (lr, and_6_out, dx);
  or or_4 (lx, lb, mx);
  and and_1 (lb, not_9_out, not_8_out, not_7_out, not_1_out);
  and and_2 (_2s, not_9_out, not_8_out, not_1_out, not_2_out);
  and and_3 (mx, not_9_out, not_3_out, not_7_out, not_6_out);
  and and_4 (sm, not_9_out, not_3_out, not_2_out, not_6_out);
  and and_5 (md, not_9_out, not_3_out, not_2_out, not_1_out);
  and and_6 (and_6_out, not_4_out, not_8_out, not_7_out, not_6_out);
  and and_7 (dx, not_4_out, not_8_out, not_2_out, not_6_out);
  not not_1 (not_1_out, not_6_out);
  not not_2 (not_2_out, not_7_out);
  not not_3 (not_3_out, not_8_out);
  not not_4 (not_4_out, not_9_out);
  or or_5 (or_7_out[3], and_8_out, and_13_out);
  or or_6 (or_7_out[1], and_18_out, and_19_out, and_20_out, and_21_out, and_22_out);
  or or_7 (or_7_out[0], and_9_out, and_10_out, and_11_out, and_12_out);
  and and_8 (and_8_out, or_9_out, state[3], not_8_out, not_7_out);
  or or_8 (or_7_out[2], and_14_out, and_15_out, and_16_out, and_17_out);
  and and_9 (and_9_out, state[3], not_8_out, not_7_out, not_6_out);
  and and_10 (and_10_out, not_9_out, state[1], not_6_out);
  and and_11 (and_11_out, not_9_out, state[1], state[2]);
  and and_12 (and_12_out, not_8_out, not_7_out, not_6_out, go);
  or or_9 (or_9_out, eq1, not_6_out);
  and and_13 (and_13_out, not_9_out, eq, not_7_out, state[2], state[0]);
  and and_14 (and_14_out, not_9_out, state[0], state[1]);
  and and_15 (and_15_out, not_9_out, state[1], not_5_out);
  not not_5 (not_5_out, lt);
  and and_16 (and_16_out, not_9_out, state[1], state[2]);
  and and_17 (and_17_out, not_9_out, state[0], state[2], gr);
  and and_18 (and_18_out, not_9_out, state[1], not_6_out, lt);
  and and_19 (and_19_out, not_9_out, not_8_out, not_7_out, state[0]);
  and and_20 (and_20_out, not_9_out, not_7_out, state[2], gr);
  and and_21 (and_21_out, not_9_out, not_6_out, state[2]);
  and and_22 (and_22_out, not_7_out, state[0], not_8_out, eq1);
  not not_6 (not_6_out, state[0]);
  not not_7 (not_7_out, state[1]);
  not not_8 (not_8_out, state[2]);
  not not_9 (not_9_out, state[3]);
  Register #(.width(4)) u_state (.D(or_7_out), .en(1'b1), .Q(state), .clk(clk));  // open: clr

  assign mr = lb;
  assign sa = md;

  // Notes on the sheet:
  //   s3
  //   s4
  //   s6
  //   s7
  //   s8
  //   s10
  //   s1
  //   3     2       1       0
  //   n1
  //   n0
  //   n3
  //   n2
endmodule
