// Logisim project datapath.circ as structural Verilog: 1 circuit, main circuit main
module main (
  input  s_a,
  input  [15:0] a_i,
  input  _2_s,
  input  [15:0] cmp,
  input  l_a,
  input  m_x,
  input  [15:0] x_i,
  input  l_x,
  input  m_r,
  input  [15:0] m_i,
  input  l_m,
  input  s_m,
  input  l_r,
  input  [15:0] b_i,
  input  l_b,
  input  m_d,
  input  clk,
  input  d_x,
  output gt,
  output eq,
  output lt,
  output [15:0] result,
  output eq1
);

  wire undriven;
  wire [15:0] a_q, adder_1_out, b_q, demultiplexer_1_out0, demultiplexer_1_out1, m_q, multiplexer_1_out,
       multiplexer_2_out, multiplexer_3_out, multiplexer_4_out, multiplexer_5_out, multiplexer_6_out,
       multiplexer_7_out, multiplexer_8_out, negator_1_out, negator_2_out, negator_3_out, x_q;

  Negator #(.width(16)) negator_1 (.in(a_q), .out(negator_1_out));
  Multiplexer #(.width(16)) multiplexer_1 (
    .in0(a_i), .in1(demultiplexer_1_out1), .out(multiplexer_1_out), .sel(s_a));  // open: en
  Multiplexer #(.width(16)) multiplexer_2 (.in0(x_i), .in1(16'h1), .out(multiplexer_2_out), .sel(m_x));  // open: en
  Multiplexer #(.width(16)) multiplexer_3 (
    .in0(m_i), .in1(demultiplexer_1_out0), .out(multiplexer_3_out), .sel(s_m));  // open: en
  Multiplexer #(.width(16)) multiplexer_4 (
    .in0(multiplexer_1_out), .in1(negator_1_out), .out(multiplexer_4_out), .sel(_2_s), .en(undriven));
  Multiplexer #(.width(16)) multiplexer_5 (
    .in0(multiplexer_6_out), .in1({16{1'b0}}), .out(multiplexer_5_out), .sel(m_r));  // open: en
  Register #(.width(16)) a (.D(multiplexer_4_out), .en(l_a), .Q(a_q), .clk(clk));  // open: clr
  Register #(.width(16)) x (.D(multiplexer_2_out), .en(l_x), .Q(x_q), .clk(clk));  // open: clr
  Register #(.width(16)) m (.D(multiplexer_3_out), .en(l_m), .Q(m_q), .clk(clk));  // open: clr
  Register #(.width(16)) b (.D(b_i), .en(l_b), .Q(b_q), .clk(clk));  // open: clr
  Register #(.width(16)) reg_r (.D(multiplexer_5_out), .en(l_r), .Q(result), .clk(clk));  // open: clr
  Comparator #(.width(16)) comparator_1 (.a(a_q), .b(cmp), .gt(gt), .eq(eq), .lt(lt));
  Multiplexer #(.width(16)) multiplexer_6 (
    .in0(m_q), .in1(negator_2_out), .out(multiplexer_6_out), .sel(d_x));  // open: en
  Negator #(.width(16)) negator_2 (.in(m_q), .out(negator_2_out));
  Comparator #(.width(16)) comparator_2 (.a(x_q), .b(16'h1), .eq(eq1));  // open: gt, lt
  Negator #(.width(16)) negator_3 (.in(16'h1), .out(negator_3_out));
  Multiplexer #(.width(16)) multiplexer_7 (.in0(m_q), .in1(a_q), .out(multiplexer_7_out), .sel(m_d));  // open: en
  Multiplexer #(.width(16)) multiplexer_8 (
    .in0(b_q), .in1(negator_3_out), .out(multiplexer_8_out), .sel(m_d));  // open: en
  Demultiplexer #(.width(16)) demultiplexer_1 (
    .out0(demultiplexer_1_out0), .out1(demultiplexer_1_out1), .in(adder_1_out), .sel(m_d));  // open: en
  Adder #(.width(16)) adder_1 (.a(multiplexer_7_out), .b(multiplexer_8_out), .out(adder_1_out));  // open: cin, cout

  // Notes on the sheet:
  //   gt
  //   eq
  //   lt
  //   eq1
endmodule
