// Logisim project main.circ as structural Verilog: 1 circuit, main circuit main
module main (
  input  [15:0] b,
  input  [15:0] a,
  output [3:0] out_3,
  output [15:0] result
);

  wire button_1_out, clock_1_out, main_1__2s, main_1_dx, main_1_la, main_1_lb, main_1_lm, main_1_lr,
       main_1_lx, main_1_md, main_1_mr, main_1_mx, main_1_sa, main_1_sm, main_2_eq, main_2_eq1, main_2_gt,
       main_2_lt;

  Button button_1 (.out(button_1_out));
  Clock clock_1 (.out(clock_1_out));
  cu_main main_1 (
    .mr(main_1_mr), .lb(main_1_lb), .lx(main_1_lx), .clk(clock_1_out), .la(main_1_la), .eq(main_2_eq),
    ._2s(main_1__2s), .mx(main_1_mx), .lt(main_2_lt), .state(out_3), .lm(main_1_lm), .sm(main_1_sm),
    .md(main_1_md), .sa(main_1_sa), .gr(main_2_gt), .lr(main_1_lr), .dx(main_1_dx), .eq1(main_2_eq1),
    .go(button_1_out));
  datapath_main main_2 (
    .s_a(main_1_sa), .gt(main_2_gt), .eq(main_2_eq), .lt(main_2_lt), .a_i(a), ._2_s(main_1__2s),
    .cmp({16{1'b0}}), .l_a(main_1_la), .m_x(main_1_mx), .x_i({16{1'b0}}), .l_x(main_1_lx), .m_r(main_1_mr),
    .m_i({16{1'b0}}), .l_m(main_1_lm), .s_m(main_1_sm), .l_r(main_1_lr), .b_i(b), .l_b(main_1_lb),
    .m_d(main_1_md), .clk(clock_1_out), .eq1(main_2_eq1), .d_x(main_1_dx), .result(result));
endmodule
